# Fritzing sketch fritzing (saved by Fritzing 0.9.2b)
circuit board: 2.71329cm x 5.52066cm
breadboards: 1

parts:
  Q1 = MOSFET-NCHANNEL [package=to-92]
  J1 = female pin header, 5 pins [form="♀ (female)"]
  J2 = double row female pin header, 10 pins [form="♀ (female)"]
  Q2 = MOSFET-NCHANNEL [package=to-92]
  Q3 = MOSFET-NCHANNEL [package=to-92]
  Q4 = MOSFET-NCHANNEL [package=to-92]
  Q5 = MOSFET-NCHANNEL [package=to-92]
  Bauteil4 = Arduino Micro (Rev3)
  J3 = female pin header, 1 pin [form="♀ (female)"]
  J4 = female pin header, 1 pin [form="♀ (female)"]
  J5 = female pin header, 1 pin [form="♀ (female)"]
  J6 = female pin header, 1 pin [form="♀ (female)"]

nets:
  N1: Q1.D, J2.pin4
  N2: Q1.S, Bauteil4.D6_PWM/A7
  N3: Q1.G, J1.pin1, Q2.G, Q3.G, Q4.G, Q5.G, Bauteil4.GND, J6.pin1
  N4: J1.pin2, J2.pin5, Bauteil4.5V
  N5: J1.pin3, Bauteil4.D12_PWM/A11
  N6: J1.pin5, Bauteil4.D11_PWM
  N7: J2.pin1, Bauteil4.D8_PWM/A8
  N8: J2.pin2, Bauteil4.D7
  N9: J2.pin3, Q3.D, J4.pin1
  N10: J2.pin7, Q5.D
  N11: J2.pin8, Q2.D, J3.pin1
  N12: J2.pin9, Q4.D, J5.pin1
  N13: J2.pin10, Bauteil4.D9_PWM/A9
  N14: Q2.S, Bauteil4.D5_PWM
  N15: Q3.S, Bauteil4.D4_PWM/A6
  N16: Q4.S, Bauteil4.D3/SCL
  N17: Q5.S, Bauteil4.D2/SDA
